# Fritzing sketch Schaltplan (saved by Fritzing 0.9.3b)
breadboards: 2

parts:
  S1 = H-Bridge with L298N
  Bauteil2 = Arduino Uno (Rev3) - ICSP
  R1 = Resistor [tolerance=±5% resistance=220 package=THT]
  BAT1 = BC9VPC [package=bc9vpc]
  M1 = DC Motor
  LED1 = RGB LED (com. anode, rbg) [package="5 mm [THT]"]
  R2 = Resistor [tolerance=±5% resistance=220 package=THT]
  R3 = Resistor [tolerance=±5% resistance=220 package=THT]
  LED2 = RGB LED (com. anode, rbg) [package="5 mm [THT]"]
  M2 = DC Motor
  J3 = Basic Servo
  J4 = Basic Servo

nets:
  N1: S1.12V, BAT1.V+
  GND: S1.GND, Bauteil2.GND, BAT1.V-, J3.gnd, J4.gnd
  5V: S1.5V, Bauteil2.5V, LED1.common_anode, LED2.blue_cathode, J3.vcc, J4.vcc
  N2: S1.ENA, Bauteil2.D5_PWM
  N3: S1.IN1, Bauteil2.D6_PWM
  N4: S1.IN2, Bauteil2.D7
  N5: S1.IN3, Bauteil2.D8
  N6: S1.IN4, Bauteil2.D9_PWM
  N7: S1.ENB, Bauteil2.D10_PWM/SS
  N8: S1.M1-01, M2.pin_2
  N9: S1.M1-02, M2.pin_1
  N10: S1.M2-01, M1.pin_1
  N11: S1.M2-02, M1.pin_2
  N12: Bauteil2.A1, R2.Pin_1
  N13: Bauteil2.A2, R1.Pin_1
  N14: Bauteil2.A3, R3.Pin_1
  N15: Bauteil2.A4/SDA, J4.pulse
  N16: Bauteil2.A5/SCL, J3.pulse
  N17: R1.Pin_0, LED1.blue_cathode, LED2.common_anode
  N18: LED1.red_cathode, R2.Pin_0, LED2.green_cathode
  N19: LED1.green_cathode, R3.Pin_0, LED2.red_cathode

custom parts:
  H-Bridge with L298N: h-bridge
